# Fritzing sketch Untitled Sketch 3 (saved by Fritzing 0.9.3b)
breadboards: 1

parts:
  S1 = Pushbutton [package="[THT]"]
  R1 = Resistor [tolerance=±5% resistance=220 package=THT]
  LED1 = LED - 5mm [color="Blue (470nm)" package="5 mm [THT]"]
  R2 = Resistor [tolerance=±5% resistance=220 package=THT]
  R3 = Resistor [tolerance=±5% resistance=220 package=THT]
  LED2 = smd LED [color="Infrared (850nm)" package="0603 [SMD]"]
  LED3 = smd LED [color="Red (633nm)" package="1206 [SMD]"]
  R4 = Resistor [tolerance=±5% resistance=220 package=THT]
  R5 = Resistor [tolerance=±5% resistance=220 package=THT]
  S2 = Pushbutton [package="[THT]"]
  Composant1 = Arduino Uno (Rev3)
  LCD1 = LCD screen  # not connected

nets:
  N1: S1.Pin_1, S1.Pin_2, S2.Pin_3, S2.Pin_4, Composant1.5V
  N2: S1.Pin_3, S1.Pin_4, R1.Pin_1, Composant1.D9_PWM
  N3: R1.Pin_0, LED1.cathode, LED2.cathode, LED3.cathode, R5.Pin_1, Composant1.GND
  N4: LED1.anode, R2.Pin_1
  N5: R2.Pin_0, Composant1.D11_PWM/MOSI
  N6: R3.Pin_0, Composant1.D12/MISO
  N7: R3.Pin_1, LED2.anode
  N8: LED3.anode, R4.Pin_1
  N9: R4.Pin_0, Composant1.D13/SCK
  N10: R5.Pin_0, S2.Pin_1, S2.Pin_2, Composant1.D10_PWM/SS
